# Fritzing sketch conexiones (saved by Fritzing 0.9.9b)
breadboards: 1

parts:
  Driver1 = 28BYJ-48 Driver Module [part_number=ULN2003 package=THT]
  Driver2 = 28BYJ-48 Driver Module [part_number=ULN2003 package=THT]
  SM1 = 28BYJ-48 Stepper Motor [part_number=28BYJ-48]
  SM2 = 28BYJ-48 Stepper Motor [part_number=28BYJ-48]
  Part1 = Arduino Nano (Rev3.0) (ICSP)
  buzzer1 = Passive buzzer [package=THT]
  Keypad1 = EscornaKeypad [package=THT]
  S1 = Toggle Switch [package=THT]
  VCC1 = Battery
  SERVO1 = Tower Pro SG90 servo [part_number=101246]

nets:
  N1: Driver1.IN1, Part1.D5
  N2: Driver1.IN2, Part1.D4
  N3: Driver1.IN3, Part1.D3
  N4: Driver1.IN4, Part1.D2
  GND: Driver1.GND, Driver2.GND, Part1.GND, buzzer1.pin1, Keypad1.GND, VCC1.-, SERVO1.GND
  VIN: Driver1.Vmotor, Driver2.Vmotor, Part1.VIN, S1.L2, SERVO1.+5V
  N5: Driver1.blue-pin, SM1.blue-pin
  N6: Driver1.pink-pin, SM1.pink-pin
  N7: Driver1.yellow-pin, SM1.yellow-pin
  N8: Driver1.orange-pin, SM1.orange-pin
  N9: Driver1.red-pin, SM1.red-pin
  N10: Driver2.IN1, Part1.D9
  N11: Driver2.IN2, Part1.D8
  N12: Driver2.IN3, Part1.D7
  N13: Driver2.IN4, Part1.D6
  N14: Driver2.blue-pin, SM2.blue-pin
  N15: Driver2.pink-pin, SM2.pink-pin
  N16: Driver2.yellow-pin, SM2.yellow-pin
  N17: Driver2.orange-pin, SM2.orange-pin
  N18: Driver2.red-pin, SM2.red-pin
  N19: Part1.D10, buzzer1.pin2
  N20: Part1.D11/MOSI, SERVO1.Signal
  N21: Part1.A4, Keypad1.SIG
  N22: S1.COM, VCC1.+

custom parts:
  28BYJ-48 Driver Module: ULN2003 Driver Module for the 28BYJ-48 Unipolar Stepper Motor LED A - Blue wire - Bottom coil left LED B - Pink wire - Top coil left LED C - Yellow wire - Bottom coil right LED D - Orange wire - Top coil right Common rail - red Connector pins: blue - pink - yellow - orange - red Control pins - IN1 to IN4 Power pins - GND & Vmotor (5-12V) On/Off jumper (if removed, power to motor is cut).
  28BYJ-48 Stepper Motor: Unipolar Stepper Motor 28BYJ-48 Top coil - pink & orange Bottom coil - blue & yellow Common rail - red Connector pins: blue - pink - yellow - orange - red
  Passive buzzer: Passive buzzer 12 mm, 3-5 V
  EscornaKeypad: Keypad with 5 push buttons for the Escornabot robot: escornabot.org.
  Tower Pro SG90 servo: Original file by John De Cristofaro http://www.adafruit.com/products/1449 Adafruit Feedback Servo (Small) Edited by: e-radionica.com 28/9/2015
